# Fritzing sketch projeto-02 (saved by Fritzing 0.9.3b)
breadboards: 1

parts:
  Componente1 = Arduino Uno (Rev3)
  LED1 = RGB LED (com. cathode, rgb) [package="5 mm [THT]"]

nets:
  N1: Componente1.GND, LED1.common_cathode
  N2: Componente1.D3_PWM, LED1.blue_anode
  N3: Componente1.D5_PWM, LED1.green_anode
